# Fritzing sketch autofritzing (saved by Fritzing 0.9.10b)
breadboards: 4

parts:
  Part1 = Adafruit HUZZAH32 ESP32 Feather [part_number="Adafruit #3405"]
  HC-SR04_Sensor_1 = HC-SR04 Ultrasonic Distance Sensor
  HC-SR04_Sensor_2 = HC-SR04 Ultrasonic Distance Sensor
  IC1 = Voltage Regulator [package=78xxl]
  VCC1 = Battery block 9V
  VCC2 = Battery block 9V
  Part2 = Adafruit DC+Stepper FeatherWing [part_number="Adafruit #2927"]
  M1 = gear-motor
  M2 = gear-motor
  Part3 = Adafruit HUZZAH32 ESP32 Feather [part_number="Adafruit #3405"]
  Mod1 = KY-023 Dual Axis Joystick Module [package="Breakout board"]

nets:
  N1: Part1.IO21, Part2.G
  N2: Part1.IO17, Part2.TX
  N3: Part1.IO16, Part2.RX
  N4: Part1.MISO, Part2.MISO
  N5: Part1.MOSI, Part2.MOSI
  N6: Part1.SCK, Part2.SCK
  N7: Part1.A5_IO4, Part2.F
  N8: Part1.A4_IO36, Part2.E
  N9: Part1.A3_I39, Part2.D
  N10: Part1.A2_I34, Part2.C
  N11: Part1.A1_DAC1, Part2.B
  N12: Part1.A0_DAC2, Part2.A
  GND: Part1.GND, HC-SR04_Sensor_1.GND, HC-SR04_Sensor_2.GND, IC1.GND, VCC1.-, Part2.GND
  N13: Part1.N/C, Part2.AREF
  3.3V: Part1.3.3V, Part2.+3.3V
  N14: Part1.RESET, Part2.RESET
  N15: Part1.VBAT, Part2.VBAT
  N16: Part1.EN, Part2.EN
  N17: Part1.VBUS, Part2.USB
  N18: Part1.IO13_A12, Part2.N
  N19: Part1.IO12_A11, Part2.M
  N20: Part1.IO27_A10, Part2.L
  N21: Part1.IO33_A9, HC-SR04_Sensor_2.TRIG, Part2.K
  N22: Part1.IO15_A8, HC-SR04_Sensor_2.ECHO, Part2.J
  N23: Part1.IO32_A7, HC-SR04_Sensor_1.TRIG, Part2.I
  N24: Part1.IO14_A6, HC-SR04_Sensor_1.ECHO, Part2.H
  N25: Part1.SCL, Part2.SCL
  N26: Part1.SDA, Part2.SDA
  VCC: HC-SR04_Sensor_1.VCC, HC-SR04_Sensor_2.VCC, IC1.OUT
  N27: VCC2.+, Part2.VMOTOR
  N28: Part2.M1B, M2.pin_1
  N29: Part2.M1A, M2.pin_2
  N30: Part2.M2A, M1.pin_1
  N31: Part2.M2B, M1.pin_2
  GND_2: Part3.GND, Mod1.GND
  3.3V_2: Part3.3.3V, Mod1.+5V
  N32: Part3.IO15_A8, Mod1.VRx
  N33: Part3.IO32_A7, Mod1.VRy
  N34: Part3.IO14_A6, Mod1.SW

custom parts:
  Adafruit DC+Stepper FeatherWing: This is the DC Motor + Stepper FeatherWing which will let you use 2 x bi-polar stepper motors or 4 x brushed DC motorx (or 1 stepper and 2 DC motors). Using our Feather Stacking Headers or Feather Female Headers you can connect a FeatherWing on top or bottom of your Feather board and let the board take flight! The original Adafruit Motorshield Kit is one of our most beloved kits, which is why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
  KY-023 Dual Axis Joystick Module: KY-023 Dual-Axis Joystick Module.
